// Logisim project VeryHardWareRISCV.circ as structural Verilog: 2 circuits, main circuit RISCV
module RISCV (
);

  wire and_1_out, clk, clock_1_out, halt, isBEQ, JAL, MR, MW, op5, R_r1_____R_r2, RW, selImm, xor_1_out;
  wire [1:0] opALU;
  wire [2:0] funct3, TYPE;
  wire [3:0] op;
  wire [4:0] rd, rs1, rs2;
  wire [6:0] imm25, instdecoder_1_p1;
  wire [31:0] adder_1_out, alu_1_p4, data_memory_32_1_p6, imm, instruction, multiplexer_1_out,
       multiplexer_2_out, pc_1_p3, PC___4, register_file_1_p4, register_file_1_p7, register_file_1_p8;

  Clock #(.highDuration(8), .lowDuration(8)) clock_1 (.out(clock_1_out));
  and and_1 (and_1_out, isBEQ, R_r1_____R_r2);
  Adder #(.width(32)) adder_1 (.a(imm), .b(pc_1_p3), .out(adder_1_out));  // open: cin, cout
  // ClockGen clockgen_1: pin names not known; wires that end beside it: halt, clock_1_out, clk
  xor xor_1 (xor_1_out, and_1_out, JAL);
  Multiplexer #(.width(32), .enable("false")) multiplexer_1 (
    .in0(PC___4), .in1(adder_1_out), .out(multiplexer_1_out), .sel(xor_1_out));
  // Register_file register_file_1: pin names not known; wires that end beside it: rs1, rs2, rd, register_file_1_p4, clk, RW, register_file_1_p7, register_file_1_p8
  // PC pc_1: pin names not known; wires that end beside it: multiplexer_1_out, clk, pc_1_p3
  Comparator #(.width(32)) comparator_1 (
    .a(register_file_1_p7), .b(register_file_1_p8), .eq(R_r1_____R_r2));  // open: gt, lt
  Adder #(.width(32)) adder_2 (.a(32'h4), .b(pc_1_p3), .out(PC___4));  // open: cin, cout
  // Probe on pc_1_p3
  Multiplexer #(.width(32), .enable("false")) multiplexer_2 (
    .in0(register_file_1_p8), .in1(imm), .out(multiplexer_2_out), .sel(selImm));
  // Instruction_memory instruction_memory_1: pin names not known; wires that end beside it: pc_1_p3, instruction, instruction
  // ALU alu_1: pin names not known; wires that end beside it: register_file_1_p7, multiplexer_2_out, op, alu_1_p4
  // Probe on instruction
  // InstDecoder instdecoder_1: pin names not known; wires that end beside it: instdecoder_1_p1, rd, funct3, rs1, rs2, imm25
  // Data_Memory_32 data_memory_32_1: pin names not known; wires that end beside it: alu_1_p4, register_file_1_p8, clk, MR, MW, data_memory_32_1_p6
  Control_Unit control_unit_1 (
    .OPC(instdecoder_1_p1), .TYPE(TYPE), .RW(RW), .MR(MR), .MW(MW), .isHALT(halt), .isJAL(JAL),
    .ALUSrc(selImm), .opALU(opALU), .isBEQ(isBEQ), .op5(op5));
  Multiplexer #(.select(2), .width(32), .enable("false")) multiplexer_3 (
    .in0(alu_1_p4), .in1(data_memory_32_1_p6), .in2(PC___4), .in3(PC___4), .out(register_file_1_p4),
    .sel({JAL, MR}));
  // Control_ALU control_alu_1: pin names not known; wires that end beside it: imm25, funct3, op5, opALU, op
  // Extender extender_1: pin names not known; wires that end beside it: instruction, TYPE, imm
endmodule

module Control_Unit (
  input  [6:0] OPC,
  output [2:0] TYPE,
  output RW,
  output MR,
  output MW,
  output isHALT,
  output isJAL,
  output ALUSrc,
  output [1:0] opALU,
  output isBEQ,
  output op5
);

  wire [8:8] rom_1_data;

  ROM #(.addrWidth(7), .dataWidth(12)) rom_1 (
    .addr(OPC), .data({isBEQ, opALU, rom_1_data[8], isJAL, isHALT, MW, MR, RW, TYPE}));  // open: sel
  not not_1 (ALUSrc, rom_1_data[8]);

  assign op5 = OPC[5];

  // Notes on the sheet:
  //   contents of rom_1 (hex, n*v repeats v):
  //   0 0 0 18 15*0 408 15*0 21 15*0 508 47*0 802 11*0 8c 15*0 40
endmodule
